# Fritzing sketch bomb2.0 (saved by Fritzing 0.7.12b)
breadboards: 1

parts:
  GREENLED = LED - 5mm [color="Green (570nm)" package="5 mm [THT]"]
  REDLED = LED - 5mm [color="Red (633nm)" package="5 mm [THT]"]
  R1 = Rotary Potentiometer (Small) [maximum_resistance=10kΩ]
  SPKR1 = Loudspeaker
  Arduino1 = Arduino
  LCD1 = LCD screen
  R7 = Resistor [tolerance=±5% resistance=220 package=THT]
  R8 = Resistor [tolerance=±5% resistance=220 package=THT]
  Mosfet_Connection = screw terminal, 3 pins
  D_Button = Pushbutton [package="[THT]"]
  C_Button = Pushbutton [package="[THT]"]
  KEYBOARD = Generic male header - 8 pins [package=THT]

nets:
  GND: GREENLED.cathode, REDLED.cathode, R1.leg2, SPKR1.pin2, LCD1.VSS, LCD1.R/W, LCD1.LED-, Mosfet_Connection.pin1
  N1: GREENLED.anode, R8.Pin_1
  N2: REDLED.anode, R7.Pin_1
  5V: R1.leg1, Arduino1.+5V, LCD1.VDD, LCD1.LED+, Mosfet_Connection.pin2
  N3: R1.wiper, LCD1.V0
  N4: SPKR1.pin1, Arduino1.D8
  N5: Arduino1.D13, D_Button.Pin_1, D_Button.Pin_2, KEYBOARD.pin7
  N6: Arduino1.D12, C_Button.Pin_2, KEYBOARD.pin8
  N7: Arduino1.D11, R7.Pin_0
  N8: Arduino1.D10, R8.Pin_0
  N9: Arduino1.D9, Mosfet_Connection.pin3
  N10: Arduino1.D7, LCD1.RS
  N11: Arduino1.D6, LCD1.E
  N12: Arduino1.D5, LCD1.DB4
  N13: Arduino1.D4, LCD1.DB5
  N14: Arduino1.D3, LCD1.DB6
  N15: Arduino1.D2, LCD1.DB7
  N16: Arduino1.A0, KEYBOARD.pin1
  N17: Arduino1.A1, KEYBOARD.pin2
  N18: Arduino1.A2, KEYBOARD.pin3
  N19: Arduino1.A3, D_Button.Pin_3, D_Button.Pin_4, C_Button.Pin_3, C_Button.Pin_4, KEYBOARD.pin4
  N20: Arduino1.A4, KEYBOARD.pin5
  N21: Arduino1.A5, KEYBOARD.pin6

notes:
  keyboard matrix 4x4
  'C' or Left button Connected to pin 4 & 7
  'D' or Right button
  Conected to pin 4 & 8
